// Logisim project Synchronous 4-bit Counter (student numbers).circ as structural Verilog: 1 circuit, main circuit main
module main (
  output out_1,
  output out_2,
  output out_3,
  output out_4
);

  wire and_1_out, and_2_out, and_3_out, and_4_out, and_5_out, and_6_out, and_7_out, clock_1_out, or_1_out,
       or_2_out, or_3_out, TA_qn, TB_qn, TC_qn, TD_qn;

  Clock clock_1 (.out(clock_1_out));
  T_Flip_Flop TD (.clk(clock_1_out), .T(or_2_out), .Q(out_4), .Qn(TD_qn));  // open: preset, reset, en
  T_Flip_Flop TC (.clk(clock_1_out), .T(or_1_out), .Q(out_3), .Qn(TC_qn));  // open: preset, reset, en
  T_Flip_Flop TB (.clk(clock_1_out), .T(out_1), .Q(out_2), .Qn(TB_qn));  // open: preset, reset, en
  T_Flip_Flop TA (.clk(clock_1_out), .T(or_3_out), .Q(out_1), .Qn(TA_qn));  // open: preset, reset, en
  and and_1 (and_1_out, TA_qn, TB_qn);
  and and_2 (and_2_out, TA_qn, TC_qn);
  or or_1 (or_1_out, and_2_out, and_1_out, and_3_out);
  and and_3 (and_3_out, TB_qn, TC_qn, out_4);
  or or_2 (or_2_out, and_4_out, and_5_out);
  and and_4 (and_4_out, out_3, out_2);
  and and_5 (and_5_out, TB_qn, out_1, TD_qn);
  and and_6 (and_6_out, out_2, TC_qn, TD_qn);
  and and_7 (and_7_out, TB_qn, out_4, TA_qn);
  or or_3 (or_3_out, and_6_out, and_7_out);
endmodule
