// Logisim project Synchronous 4-bit Counters.circ as structural Verilog: 1 circuit, main circuit main
module main (
  output out_1,
  output out_2,
  output out_3,
  output out_4
);

  wire and_1_out, and_2_out, and_3_out, clock_1_out, or_1_out, TA_qn, TB_qn;

  Clock clock_1 (.out(clock_1_out));
  T_Flip_Flop TD (.clk(clock_1_out), .T(1'b1), .Q(out_4));  // open: Qn, preset, reset, en
  T_Flip_Flop TC (.clk(clock_1_out), .T(out_4), .Q(out_3));  // open: Qn, preset, reset, en
  T_Flip_Flop TB (.clk(clock_1_out), .T(or_1_out), .Q(out_2), .Qn(TB_qn));  // open: preset, reset, en
  and and_1 (and_1_out, out_4, out_3);
  T_Flip_Flop TA (.clk(clock_1_out), .T(and_1_out), .Q(out_1), .Qn(TA_qn));  // open: preset, reset, en
  and and_2 (and_2_out, out_1, TB_qn, out_3, out_4);
  and and_3 (and_3_out, TA_qn, out_2, out_3, out_4);
  or or_1 (or_1_out, and_2_out, and_3_out);
endmodule
